// Logisim project Conway.circ as structural Verilog: 1 circuit, main circuit main
module main (
  input  Set_D_In,
  input  Row,
  input  Column,
  input  NE2,
  input  E3,
  input  Lock,
  output Read_D_Out,
  output State_Out
);

  wire and_1_out, and_2_out, and_3_out, and_4_out, and_5_out, and_6_out, and_7_out, and_8_out, and_9_out,
       and_10_out, and_11_out, and_12_out, and_14_out, Btn_Invert_out, clock_1_out, D_In_q, D_Out_qn,
       not_1_out, not_2_out, not_3_out, not_4_out, or_1_out, or_2_out, or_3_out, or_4_out, or_5_out, or_6_out;

  Clock clock_1 (.out(clock_1_out));
  Button Btn_Invert (.out(Btn_Invert_out));
  not not_1 (not_1_out, clock_1_out);
  not not_2 (not_2_out, Lock);
  and and_1 (and_1_out, Row, Column);
  and and_2 (and_2_out, NE2, not_1_out);
  not not_3 (not_3_out, Btn_Invert_out);
  and and_3 (and_3_out, and_1_out, clock_1_out);
  and and_4 (and_4_out, and_2_out, Lock);
  and and_5 (and_5_out, not_2_out, Btn_Invert_out);
  and and_6 (and_6_out, not_3_out, not_2_out);
  and and_7 (and_7_out, D_Out_qn, not_2_out);
  and and_8 (and_8_out, E3, Lock);
  or or_1 (or_1_out, and_4_out, and_5_out);
  and and_9 (and_9_out, Set_D_In, and_1_out);
  not not_4 (not_4_out, and_1_out);
  or or_2 (or_2_out, and_7_out, and_8_out);
  D_Flip_Flop D_In (.D(or_4_out), .clk(or_3_out), .Q(D_In_q));  // open: Qn, preset, reset
  or or_3 (or_3_out, and_3_out, or_1_out);
  and and_10 (and_10_out, clock_1_out, Lock);
  or or_4 (or_4_out, and_9_out, and_11_out);
  and and_11 (and_11_out, not_4_out, or_2_out);
  D_Flip_Flop D_Out (.D(D_In_q), .clk(or_6_out), .Q(State_Out), .Qn(D_Out_qn));  // open: preset, reset
  or or_5 (or_5_out, and_10_out, and_6_out);
  and and_12 (and_12_out, and_1_out, not_1_out);
  and and_13 (Read_D_Out, and_1_out, State_Out);
  LED led_1 (.in(State_Out));
  and and_14 (and_14_out, not_4_out, or_5_out);
  or or_6 (or_6_out, and_14_out, and_12_out);
endmodule
